// Logisim project Somadores.circ as structural Verilog: 14 circuits, main circuit main
module main (
  input  in_1,
  input  R___1___W___0,
  input  [3:0] in_3,
  output out_4,
  output out_5
);

  wire clock_1_out, clock_2_out, clock_3_out, not_1_out, not_2_out;
  wire [3:0] ac_1_s, counter_1_q, mux_1_out_4, ram_1_data, ula_1_out_6;
  wire [7:0] rom_1_data;

  not not_1 (not_1_out, in_1);
  Counter #(.width(4), .max('hf)) counter_1 (
    .load(in_1), .D(in_3), .count(not_1_out), .Q(counter_1_q), .clk(clock_1_out));  // open: carry, clr
  Clock clock_1 (.out(clock_1_out));
  Clock clock_2 (.out(clock_2_out));
  ROM #(.addrWidth(4)) rom_1 (.addr(counter_1_q), .data(rom_1_data));  // open: sel
  // Probe on ac_1_s
  ULA ula_1 (
    .D(rom_1_data[4]), .A(ac_1_s), .B(mux_1_out_4), .Overflow(out_4), .in_4(rom_1_data[7:5]),
    .out_6(ula_1_out_6), .Zero(out_5));
  AC ac_1 (.Clock(clock_2_out), .E(ula_1_out_6), .S(ac_1_s));
  MUX mux_1 (.e(rom_1_data[3:0]), .c(rom_1_data[4]), .D(ram_1_data), .out_4(mux_1_out_4));
  // Probe on mux_1_out_4
  // Probe on ula_1_out_6
  // Probe on ram_1_data
  Clock clock_3 (.out(clock_3_out));
  RAM #(.addrWidth(4), .dataWidth(4)) ram_1 (
    .addr(rom_1_data[3:0]), .data(ram_1_data), .clk(clock_3_out), .ld(R___1___W___0));  // open: sel, clr
  not not_2 (not_2_out, R___1___W___0);
  Buff buff_1 (.E(ac_1_s), .in_2(not_2_out), .S(ram_1_data));

  // Notes on the sheet:
  //   contents of rom_1 (hex, n*v repeats v):
  //   1 15*21
endmodule

module Somador_1Bit (
  input  A,
  input  B,
  input  C,
  output S,
  output Vai_1
);

  wire and_1_out, and_2_out, or_1_out, xor_1_out;

  xor xor_1 (xor_1_out, C, B);
  and and_1 (and_1_out, C, B);
  or or_1 (or_1_out, C, B);
  and and_2 (and_2_out, or_1_out, A);
  xor xor_2 (S, xor_1_out, A);
  or or_2 (Vai_1, and_1_out, and_2_out);
endmodule

module Somador_4Bits (
  input  [3:0] A,
  input  [3:0] B,
  output Overflow,
  output [3:0] Saida
);

  wire somador_1bit_2_vai_1, somador_1bit_3_vai_1, somador_1bit_4_vai_1;

  // Probe on B
  Somador_1Bit somador_1bit_1 (.S(Saida[3]), .Vai_1(Overflow), .A(A[3]), .B(B[3]), .C(somador_1bit_2_vai_1));
  Somador_1Bit somador_1bit_2 (
    .S(Saida[2]), .Vai_1(somador_1bit_2_vai_1), .A(A[2]), .B(B[2]), .C(somador_1bit_3_vai_1));
  // Probe on Saida
  Somador_1Bit somador_1bit_3 (
    .S(Saida[1]), .Vai_1(somador_1bit_3_vai_1), .A(A[1]), .B(B[1]), .C(somador_1bit_4_vai_1));
  Somador_1Bit somador_1bit_4 (.S(Saida[0]), .Vai_1(somador_1bit_4_vai_1), .A(A[0]), .B(B[0]), .C(1'b0));
  // Probe on A
endmodule

module Subtrator_1Bit (
  input  A,
  input  B,
  input  C,
  output S,
  output Vai_1
);

  wire and_1_out, and_2_out, or_1_out, xor_1_out;

  xor xor_1 (xor_1_out, C, B);
  and and_1 (and_1_out, C, B);
  or or_1 (or_1_out, C, B);
  and and_2 (and_2_out, or_1_out, ~A);  // AND_Gate
  xor xor_2 (S, xor_1_out, A);
  or or_2 (Vai_1, and_1_out, and_2_out);
endmodule

module Subtrator_4Bit (
  input  [3:0] A,
  input  [3:0] B,
  output Overflow,
  output [3:0] Saida
);

  wire subtrator_1bit_2_vai_1, subtrator_1bit_3_vai_1, subtrator_1bit_4_vai_1;

  // Probe on B
  Subtrator_1Bit subtrator_1bit_1 (.S(Saida[3]), .Vai_1(Overflow), .A(A[3]), .B(B[3]), .C(subtrator_1bit_2_vai_1));
  Subtrator_1Bit subtrator_1bit_2 (
    .S(Saida[2]), .Vai_1(subtrator_1bit_2_vai_1), .A(A[2]), .B(B[2]), .C(subtrator_1bit_3_vai_1));
  // Probe on Saida
  Subtrator_1Bit subtrator_1bit_3 (
    .S(Saida[1]), .Vai_1(subtrator_1bit_3_vai_1), .A(A[1]), .B(B[1]), .C(subtrator_1bit_4_vai_1));
  Subtrator_1Bit subtrator_1bit_4 (.S(Saida[0]), .Vai_1(subtrator_1bit_4_vai_1), .A(A[0]), .B(B[0]), .C(1'b0));
  // Probe on A
endmodule

module \Rotação_Esq  (
  input  [3:0] ABCD,
  input  [1:0] XY,
  output [3:0] ABCD_2
);

  wire and_1_out, and_2_out, and_3_out, and_4_out, and_5_out, and_6_out, and_7_out, and_8_out, and_9_out;

  and and_1 (and_1_out, ~XY[1], ~XY[0], ABCD[3]);  // AND_Gate
  and and_2 (and_2_out, ~XY[1], XY[0], ABCD[2]);  // AND_Gate
  and and_3 (and_3_out, XY[1], ~XY[0], ABCD[1]);  // AND_Gate
  and and_4 (and_4_out, XY[1], XY[0], ABCD[0]);
  and and_5 (and_5_out, ~XY[1], ~XY[0], ABCD[2]);  // AND_Gate
  and and_6 (and_6_out, ~XY[1], XY[0], ABCD[1]);  // AND_Gate
  and and_7 (and_7_out, XY[1], ~XY[0], ABCD[0]);  // AND_Gate
  and and_8 (and_8_out, ~XY[1], ~XY[0], ABCD[1]);  // AND_Gate
  and and_9 (and_9_out, ~XY[1], XY[0], ABCD[0]);  // AND_Gate
  and and_10 (ABCD_2[0], ~XY[1], ~XY[0], ABCD[0]);  // AND_Gate
  or or_1 (ABCD_2[3], and_1_out, and_2_out, and_3_out, and_4_out);
  or or_2 (ABCD_2[2], and_5_out, and_6_out, and_7_out);
  or or_3 (ABCD_2[1], and_8_out, and_9_out);
endmodule

module \Rotação_Dir  (
  input  [3:0] ABCD,
  input  [1:0] XY,
  output [3:0] ABCD_2
);

  wire and_1_out, and_2_out, and_3_out, and_4_out, and_5_out, and_6_out, and_7_out, and_8_out, and_9_out;

  and and_1 (and_1_out, ~XY[1], ~XY[0], ABCD[0]);  // AND_Gate
  and and_2 (and_2_out, ~XY[1], XY[0], ABCD[1]);  // AND_Gate
  and and_3 (and_3_out, XY[1], ~XY[0], ABCD[2]);  // AND_Gate
  and and_4 (and_4_out, XY[1], XY[0], ABCD[3]);
  and and_5 (and_5_out, ~XY[1], ~XY[0], ABCD[1]);  // AND_Gate
  and and_6 (and_6_out, ~XY[1], XY[0], ABCD[2]);  // AND_Gate
  and and_7 (and_7_out, XY[1], ~XY[0], ABCD[3]);  // AND_Gate
  and and_8 (and_8_out, ~XY[1], ~XY[0], ABCD[2]);  // AND_Gate
  and and_9 (and_9_out, ~XY[1], XY[0], ABCD[3]);  // AND_Gate
  and and_10 (ABCD_2[3], ~XY[1], ~XY[0], ABCD[3]);  // AND_Gate
  or or_1 (ABCD_2[0], and_1_out, and_2_out, and_3_out, and_4_out);
  or or_2 (ABCD_2[1], and_5_out, and_6_out, and_7_out);
  or or_3 (ABCD_2[2], and_8_out, and_9_out);
endmodule

module Buff (
  input  [3:0] E,
  input  in_2,
  output [3:0] S
);

  assign S[3] = in_2 ? E[3] : 1'bz;  // Controlled_Buffer controlled_buffer_1
  assign S[1] = in_2 ? E[1] : 1'bz;  // Controlled_Buffer controlled_buffer_2
  assign S[2] = in_2 ? E[2] : 1'bz;  // Controlled_Buffer controlled_buffer_3
  assign S[0] = in_2 ? E[0] : 1'bz;  // Controlled_Buffer controlled_buffer_4
endmodule

module Decodificador_3x8 (
  input  [2:0] in_1,
  output S0,
  output S1,
  output S2,
  output S3,
  output S4,
  output S5,
  output S6,
  output S7
);

  wire not_1_out, not_2_out, not_3_out, not_4_out, not_5_out, not_6_out, not_7_out, not_8_out, not_9_out,
       not_10_out, not_11_out, not_12_out;

  not not_1 (not_1_out, in_1[2]);
  not not_2 (not_2_out, in_1[1]);
  not not_3 (not_3_out, in_1[0]);
  not not_4 (not_4_out, in_1[2]);
  not not_5 (not_5_out, in_1[1]);
  not not_6 (not_6_out, in_1[2]);
  not not_7 (not_7_out, in_1[0]);
  not not_8 (not_8_out, in_1[2]);
  not not_9 (not_9_out, in_1[1]);
  not not_10 (not_10_out, in_1[0]);
  not not_11 (not_11_out, in_1[1]);
  not not_12 (not_12_out, in_1[0]);
  and and_1 (S7, in_1[2], in_1[1], in_1[0]);
  and and_2 (S0, not_1_out, not_2_out, not_3_out);
  and and_3 (S1, not_4_out, not_5_out, in_1[0]);
  and and_4 (S2, not_6_out, in_1[1], not_7_out);
  and and_5 (S3, not_8_out, in_1[1], in_1[0]);
  and and_6 (S4, in_1[2], not_9_out, not_10_out);
  and and_7 (S5, in_1[2], not_11_out, in_1[0]);
  and and_8 (S6, in_1[2], in_1[1], not_12_out);
endmodule

module Or_4Bits (
  input  [3:0] A,
  input  [3:0] B,
  output [3:0] Saida
);

  // Probe on B
  or or_1 (Saida[3], A[3], B[3]);
  or or_2 (Saida[2], A[2], B[2]);
  // Probe on Saida
  or or_3 (Saida[1], A[1], B[1]);
  or or_4 (Saida[0], A[0], B[0]);
  // Probe on A
endmodule

module Not_4 (
  input  [3:0] E,
  output [3:0] S
);

  not not_1 (S[3], E[3]);
  not not_2 (S[1], E[1]);
  not not_3 (S[2], E[2]);

  assign S[0] = E[0];
endmodule

module ULA (
  input  D,
  input  [3:0] A,
  input  [3:0] B,
  input  [2:0] in_4,
  output Overflow,
  output [3:0] out_6,
  output Zero
);

  wire and_1_out, and_2_out, decodificador_3x8_1_s0, decodificador_3x8_1_s1, decodificador_3x8_1_s2,
       decodificador_3x8_1_s3, decodificador_3x8_1_s4, decodificador_3x8_1_s5, decodificador_3x8_1_s6,
       decodificador_3x8_1_s7, not_1_out, somador_4bits_1_overflow, subtrator_4bit_1_overflow;
  wire [3:0] buff_7_s, not_4_1_s, or_4bits_1_saida, \rotação_dir_1_abcd_2 , \rotação_esq_1_abcd_2 ,
       somador_4bits_1_saida, subtrator_4bit_1_saida;

  or or_1 (Overflow, and_1_out, and_2_out);
  Decodificador_3x8 decodificador_3x8_1 (
    .S0(decodificador_3x8_1_s0), .S1(decodificador_3x8_1_s1), .S2(decodificador_3x8_1_s2),
    .S3(decodificador_3x8_1_s3), .S4(decodificador_3x8_1_s4), .S5(decodificador_3x8_1_s5),
    .S6(decodificador_3x8_1_s6), .S7(decodificador_3x8_1_s7), .in_1(in_4));
  and and_1 (and_1_out, somador_4bits_1_overflow, decodificador_3x8_1_s1);
  and and_2 (and_2_out, subtrator_4bit_1_overflow, decodificador_3x8_1_s2);
  Somador_4Bits somador_4bits_1 (.B(B), .A(A), .Saida(somador_4bits_1_saida), .Overflow(somador_4bits_1_overflow));
  Buff buff_1 (.E(somador_4bits_1_saida), .in_2(decodificador_3x8_1_s1), .S(out_6));
  Buff buff_2 (.E(B), .in_2(decodificador_3x8_1_s0), .S(out_6));
  Subtrator_4Bit subtrator_4bit_1 (.B(B), .Overflow(subtrator_4bit_1_overflow), .A(A), .Saida(subtrator_4bit_1_saida));
  Buff buff_3 (.E(or_4bits_1_saida), .in_2(decodificador_3x8_1_s3), .S(out_6));
  Buff buff_4 (.E(subtrator_4bit_1_saida), .in_2(decodificador_3x8_1_s2), .S(out_6));
  nor nor_1 (Zero, out_6[0], out_6[1], out_6[2], out_6[3], decodificador_3x8_1_s6, decodificador_3x8_1_s7);
  Or_4Bits or_4bits_1 (.B(A), .A(B), .Saida(or_4bits_1_saida));
  Not_4 not_4_1 (.E(A), .S(not_4_1_s));
  Buff buff_5 (.E(not_4_1_s), .in_2(decodificador_3x8_1_s4), .S(out_6));
  // Probe on out_6
  not not_1 (not_1_out, D);
  \Rotação_Esq  \rotação_esq_1  (.ABCD(A), .XY(B[1:0]), .ABCD_2(\rotação_esq_1_abcd_2 ));
  \Rotação_Dir  \rotação_dir_1  (.ABCD(A), .XY(B[1:0]), .ABCD_2(\rotação_dir_1_abcd_2 ));
  Buff buff_6 (.E(buff_7_s), .in_2(decodificador_3x8_1_s5), .S(out_6));
  Buff buff_7 (.E(\rotação_esq_1_abcd_2 ), .in_2(not_1_out), .S(buff_7_s));
  Buff buff_8 (.E(\rotação_dir_1_abcd_2 ), .in_2(D), .S(buff_7_s));
endmodule

module AC (
  input  Clock,
  input  [3:0] E,
  output [3:0] S
);

  D_Flip_Flop d_ff_1 (.clk(Clock), .D(E[3]), .Q(S[3]));  // open: Qn, preset, en, reset
  D_Flip_Flop d_ff_2 (.clk(Clock), .D(E[1]), .Q(S[1]));  // open: Qn, preset, en, reset
  D_Flip_Flop d_ff_3 (.clk(Clock), .D(E[2]), .Q(S[2]));  // open: Qn, preset, en, reset
  D_Flip_Flop d_ff_4 (.clk(Clock), .D(E[0]), .Q(S[0]));  // open: Qn, preset, en, reset
endmodule

module MUX (
  input  [3:0] e,
  input  [3:0] D,
  input  c,
  output [3:0] out_4
);

  wire not_1_out;

  not not_1 (not_1_out, c);
  Buff buff_1 (.E(e), .in_2(not_1_out), .S(out_4));
  Buff buff_2 (.E(D), .in_2(c), .S(out_4));
endmodule
